// Logisim project CPU.circ as structural Verilog: 25 circuits, main circuit CPU_16_bit
module CPU_16_bit (
);

  wire buffer_1_out, clock_1_out, debug_1_clk_out, not_1_out, not_2_out, pull_resistor_2_node,
       reg_swap_logic_1_out_21, reg_swap_logic_1_out_22, reg_swap_logic_1_out_23, reg_swap_logic_1_out_24,
       reg_swap_logic_1_out_25, reg_swap_logic_1_out_26, reg_swap_logic_1_out_27, reg_swap_logic_1_out_28,
       reg_swap_logic_1_out_29, reg_swap_logic_1_out_30, reg_swap_logic_1_out_31, reg_swap_logic_1_out_32,
       reg_swap_logic_1_out_33, reg_swap_logic_1_out_34, reg_swap_logic_1_out_35, reg_swap_logic_1_out_36;
  wire [3:0] pull_resistor_1_node;
  wire [4:0] AC_A_q, AC_B_q, AC_q, controlled_buffer_16_out, controlled_buffer_17_out,
       controlled_buffer_18_out, MAR_A_q, MAR_B_q, MAR_q, OE_PC_out, PROGRAM_COUNTER_q;
  wire [7:0] REG_BANK_A_d_out, REG_BANK_A_d_out_2, REG_BANK_B_d_out, REG_BANK_B_d_out_2;
  wire [15:0] alu_16_bit_1_ofl, alu_16_bit_1_rout, controlled_buffer_2_out, IR_q, matmult8_1_ofl,
       matmult8_1_r1, matmult8_1_r2, matmult8_1_r3, matmult8_1_r4, MBR_A_q, MBR_B_q, MBR_q, O0_q, OFL_q,
       pull_resistor_3_node;
  wire [63:0] THE_DANGEROUS_ROM_data;

  ROM #(.addrWidth(9), .dataWidth(64)) THE_DANGEROUS_ROM (
    .addr({IR_q[15], IR_q[13:10], pull_resistor_1_node}), .data(THE_DANGEROUS_ROM_data));
  Pull_Resistor pull_resistor_1 (.node({IR_q[15], IR_q[13:10], pull_resistor_1_node}));
  not not_1 (not_1_out, 1'b1);
  not not_2 (not_2_out, THE_DANGEROUS_ROM_data[1]);
  Clock clock_1 (.out(clock_1_out));
  Counter #(.max('hf), .trigger("falling"), .width(4)) STEP_COUNTER (
    .clr(THE_DANGEROUS_ROM_data[0]), .load(not_1_out), .up(1'b1), .count(not_2_out), .clk(debug_1_clk_out),
    .Q(pull_resistor_1_node));  // open: D, carry
  DEBUG debug_1 (
    .WE(THE_DANGEROUS_ROM_data[9]), .CLK(clock_1_out), .DELAY(pull_resistor_3_node[9:5]),
    .EN_DELAY(THE_DANGEROUS_ROM_data[8]), .CLK_OUT(debug_1_clk_out));
  REG_SWAP_LOGIC reg_swap_logic_1 (
    .AddrA(pull_resistor_3_node[9:5]), .AddrB(pull_resistor_3_node[4:0]), .WE_A2(THE_DANGEROUS_ROM_data[32]),
    .OE_A1(THE_DANGEROUS_ROM_data[33]), .WE_A1(THE_DANGEROUS_ROM_data[34]),
    .OE_A0(THE_DANGEROUS_ROM_data[35]), .WE_A0(THE_DANGEROUS_ROM_data[36]),
    .OE_B3(THE_DANGEROUS_ROM_data[21]), .WE_B3(THE_DANGEROUS_ROM_data[22]),
    .OE_B2(THE_DANGEROUS_ROM_data[23]), .WE_B2(THE_DANGEROUS_ROM_data[24]),
    .OE_B1(THE_DANGEROUS_ROM_data[25]), .WE_B1(THE_DANGEROUS_ROM_data[26]),
    .OE_B0(THE_DANGEROUS_ROM_data[27]), .WE_B0(THE_DANGEROUS_ROM_data[28]),
    .OE_A3(THE_DANGEROUS_ROM_data[29]), .WE_A3(THE_DANGEROUS_ROM_data[30]),
    .OE_A2(THE_DANGEROUS_ROM_data[31]), .OE_SWAP_REG(THE_DANGEROUS_ROM_data[5]),
    .WE_SWAP_REG(THE_DANGEROUS_ROM_data[6]), .out_32(reg_swap_logic_1_out_32),
    .out_33(reg_swap_logic_1_out_33), .out_34(reg_swap_logic_1_out_34), .out_35(reg_swap_logic_1_out_35),
    .out_36(reg_swap_logic_1_out_36), .out_21(reg_swap_logic_1_out_21), .out_22(reg_swap_logic_1_out_22),
    .out_23(reg_swap_logic_1_out_23), .out_24(reg_swap_logic_1_out_24), .out_25(reg_swap_logic_1_out_25),
    .out_26(reg_swap_logic_1_out_26), .out_27(reg_swap_logic_1_out_27), .out_28(reg_swap_logic_1_out_28),
    .out_29(reg_swap_logic_1_out_29), .out_30(reg_swap_logic_1_out_30), .out_31(reg_swap_logic_1_out_31));
  Register #(.width(16)) IR (
    .D(controlled_buffer_2_out), .en(THE_DANGEROUS_ROM_data[47]), .clk(debug_1_clk_out), .Q(IR_q));  // open: clr
  Pull_Resistor pull_resistor_2 (.node(pull_resistor_2_node));
  assign pull_resistor_2_node = THE_DANGEROUS_ROM_data[63] ? debug_1_clk_out : 1'bz;  // Controlled_Buffer CE_PC
  Pull_Resistor pull_resistor_3 (.node(pull_resistor_3_node));
  assign pull_resistor_3_node = THE_DANGEROUS_ROM_data[46] ? IR_q : 16'bz;  // Controlled_Buffer controlled_buffer_1
  REG_BANK REG_BANK_A (
    .WE_0(reg_swap_logic_1_out_36), .OE_0(reg_swap_logic_1_out_35), .WE_1(reg_swap_logic_1_out_34),
    .OE_1(reg_swap_logic_1_out_33), .WE_2(reg_swap_logic_1_out_32), .OE_2(reg_swap_logic_1_out_31),
    .WE_3(reg_swap_logic_1_out_30), .OE_3(reg_swap_logic_1_out_29),
    .D_in({REG_BANK_A_d_out_2, REG_BANK_A_d_out}), .CLK(debug_1_clk_out),
    .D_out({REG_BANK_A_d_out_2, REG_BANK_A_d_out}));
  REG_BANK REG_BANK_B (
    .WE_0(reg_swap_logic_1_out_28), .OE_0(reg_swap_logic_1_out_27), .WE_1(reg_swap_logic_1_out_26),
    .OE_1(reg_swap_logic_1_out_25), .WE_2(reg_swap_logic_1_out_24), .OE_2(reg_swap_logic_1_out_23),
    .WE_3(reg_swap_logic_1_out_22), .OE_3(reg_swap_logic_1_out_21),
    .D_in({REG_BANK_B_d_out_2, REG_BANK_B_d_out}), .CLK(debug_1_clk_out),
    .D_out({REG_BANK_B_d_out_2, REG_BANK_B_d_out}));
  assign OE_PC_out = THE_DANGEROUS_ROM_data[62] ? PROGRAM_COUNTER_q : 5'bz;  // Controlled_Buffer OE_PC
  Counter #(.max('h1f), .trigger("falling"), .width(5)) PROGRAM_COUNTER (
    .Q(PROGRAM_COUNTER_q), .clk(pull_resistor_2_node));  // open: load, D, count, carry, up, clr
  ALU_16_bit alu_16_bit_1 (
    .OpCode(IR_q[14:10]), .A({REG_BANK_A_d_out_2, REG_BANK_A_d_out}),
    .B({REG_BANK_B_d_out_2, REG_BANK_B_d_out}), .OE(THE_DANGEROUS_ROM_data[16]), .Flag_bit(IR_q[15]),
    .Rout(alu_16_bit_1_rout), .OFL(alu_16_bit_1_ofl));  // open: Result
  assign controlled_buffer_2_out = THE_DANGEROUS_ROM_data[18] ? alu_16_bit_1_ofl : 16'bz;  // Controlled_Buffer controlled_buffer_2
  assign controlled_buffer_2_out = THE_DANGEROUS_ROM_data[20] ? alu_16_bit_1_rout : 16'bz;  // Controlled_Buffer controlled_buffer_3
  assign {REG_BANK_B_d_out_2, REG_BANK_B_d_out} = reg_swap_logic_1_out_28 ? matmult8_1_r1 : 16'bz;  // Controlled_Buffer controlled_buffer_4
  MATMULT8 matmult8_1 (
    .OE(THE_DANGEROUS_ROM_data[15]), .WE_E(reg_swap_logic_1_out_27), .WE_F(reg_swap_logic_1_out_25),
    .WE_G(reg_swap_logic_1_out_23), .WE_H(reg_swap_logic_1_out_21), .WE(THE_DANGEROUS_ROM_data[14]),
    .WE_A(reg_swap_logic_1_out_35), .WE_B(reg_swap_logic_1_out_33), .WE_C(reg_swap_logic_1_out_31),
    .WE_D(reg_swap_logic_1_out_29), .D_A(REG_BANK_A_d_out), .D_B(REG_BANK_B_d_out), .CLK(debug_1_clk_out),
    .R1(matmult8_1_r1), .R2(matmult8_1_r2), .R4(matmult8_1_r4), .R3(matmult8_1_r3), .OFL(matmult8_1_ofl));
  assign {REG_BANK_B_d_out_2, REG_BANK_B_d_out} = reg_swap_logic_1_out_26 ? matmult8_1_r2 : 16'bz;  // Controlled_Buffer controlled_buffer_5
  assign {REG_BANK_B_d_out_2, REG_BANK_B_d_out} = reg_swap_logic_1_out_24 ? matmult8_1_r3 : 16'bz;  // Controlled_Buffer controlled_buffer_6
  assign {REG_BANK_B_d_out_2, REG_BANK_B_d_out} = reg_swap_logic_1_out_22 ? matmult8_1_r4 : 16'bz;  // Controlled_Buffer controlled_buffer_7
  Pull_Resistor pull_resistor_4 (.node(OE_PC_out));
  assign {REG_BANK_B_d_out_2, REG_BANK_B_d_out} = THE_DANGEROUS_ROM_data[39] ? MBR_B_q : 16'bz;  // Controlled_Buffer controlled_buffer_8
  assign {REG_BANK_A_d_out_2, REG_BANK_A_d_out} = THE_DANGEROUS_ROM_data[50] ? MBR_A_q : 16'bz;  // Controlled_Buffer controlled_buffer_9
  assign controlled_buffer_2_out = THE_DANGEROUS_ROM_data[53] ? MBR_q : 16'bz;  // Controlled_Buffer IOE
  assign controlled_buffer_2_out = THE_DANGEROUS_ROM_data[18] ? matmult8_1_ofl : 16'bz;  // Controlled_Buffer controlled_buffer_10
  Register #(.width(5)) MAR (
    .D(OE_PC_out), .en(THE_DANGEROUS_ROM_data[45]), .clk(debug_1_clk_out), .Q(MAR_q));  // open: clr
  Register #(.width(5)) MAR_A (
    .D(pull_resistor_3_node[9:5]), .en(THE_DANGEROUS_ROM_data[43]), .clk(debug_1_clk_out), .Q(MAR_A_q));  // open: clr
  Register #(.width(5)) MAR_B (
    .D(pull_resistor_3_node[4:0]), .en(THE_DANGEROUS_ROM_data[41]), .clk(debug_1_clk_out), .Q(MAR_B_q));  // open: clr
  Register #(.width(16)) MBR_B (
    .D({REG_BANK_B_d_out_2, REG_BANK_B_d_out}), .en(THE_DANGEROUS_ROM_data[38]), .clk(debug_1_clk_out),
    .Q(MBR_B_q));  // open: clr
  Register #(.width(16)) MBR_A (
    .D({REG_BANK_A_d_out_2, REG_BANK_A_d_out}), .en(THE_DANGEROUS_ROM_data[49]), .clk(debug_1_clk_out),
    .Q(MBR_A_q));  // open: clr
  Register #(.width(16)) MBR (
    .D(controlled_buffer_2_out), .en(THE_DANGEROUS_ROM_data[52]), .clk(debug_1_clk_out), .Q(MBR_q));  // open: clr
  Register #(.width(16)) OFL (
    .D(controlled_buffer_2_out), .en(THE_DANGEROUS_ROM_data[18]), .clk(debug_1_clk_out), .Q(OFL_q));  // open: clr
  Register #(.width(16)) O0 (
    .D(controlled_buffer_2_out), .en(THE_DANGEROUS_ROM_data[20]), .clk(debug_1_clk_out), .Q(O0_q));  // open: clr
  assign {REG_BANK_B_d_out_2, REG_BANK_B_d_out} = THE_DANGEROUS_ROM_data[37] ? MBR_B_q : 16'bz;  // Controlled_Buffer controlled_buffer_11
  assign {REG_BANK_A_d_out_2, REG_BANK_A_d_out} = THE_DANGEROUS_ROM_data[48] ? MBR_A_q : 16'bz;  // Controlled_Buffer controlled_buffer_12
  assign controlled_buffer_2_out = THE_DANGEROUS_ROM_data[51] ? MBR_q : 16'bz;  // Controlled_Buffer controlled_buffer_13
  assign controlled_buffer_2_out = THE_DANGEROUS_ROM_data[17] ? OFL_q : 16'bz;  // Controlled_Buffer controlled_buffer_14
  assign controlled_buffer_2_out = THE_DANGEROUS_ROM_data[19] ? O0_q : 16'bz;  // Controlled_Buffer controlled_buffer_15
  assign controlled_buffer_16_out = THE_DANGEROUS_ROM_data[44] ? MAR_q : 5'bz;  // Controlled_Buffer controlled_buffer_16
  assign controlled_buffer_17_out = THE_DANGEROUS_ROM_data[42] ? MAR_A_q : 5'bz;  // Controlled_Buffer controlled_buffer_17
  assign controlled_buffer_18_out = THE_DANGEROUS_ROM_data[40] ? MAR_B_q : 5'bz;  // Controlled_Buffer controlled_buffer_18
  buf buffer_1 (buffer_1_out, debug_1_clk_out);
  assign controlled_buffer_16_out = THE_DANGEROUS_ROM_data[2] ? AC_q : 5'bz;  // Controlled_Buffer controlled_buffer_19
  Counter #(.max('h1f), .trigger("falling"), .width(5)) AC (
    .load(THE_DANGEROUS_ROM_data[3]), .D(OE_PC_out), .count(THE_DANGEROUS_ROM_data[2]), .Q(AC_q), .up(1'b1),
    .clk(debug_1_clk_out));  // open: carry, clr
  assign controlled_buffer_17_out = THE_DANGEROUS_ROM_data[2] ? AC_A_q : 5'bz;  // Controlled_Buffer controlled_buffer_20
  Counter #(.max('h1f), .trigger("falling"), .width(5)) AC_A (
    .load(THE_DANGEROUS_ROM_data[3]), .D(pull_resistor_3_node[9:5]), .count(THE_DANGEROUS_ROM_data[2]),
    .Q(AC_A_q), .up(1'b1), .clk(debug_1_clk_out));  // open: carry, clr
  assign controlled_buffer_18_out = THE_DANGEROUS_ROM_data[2] ? AC_B_q : 5'bz;  // Controlled_Buffer controlled_buffer_21
  Counter #(.max('h1f), .trigger("falling"), .width(5)) AC_B (
    .load(THE_DANGEROUS_ROM_data[3]), .D(pull_resistor_3_node[4:0]), .count(THE_DANGEROUS_ROM_data[2]),
    .Q(AC_B_q), .up(1'b1), .clk(buffer_1_out));  // open: carry, clr
  BUS_TERM_ADDR bus_term_addr_1 (
    .SELECT_2(THE_DANGEROUS_ROM_data[12]), .SELECT_1(THE_DANGEROUS_ROM_data[13]),
    .WE(THE_DANGEROUS_ROM_data[11]), .OE_Data(THE_DANGEROUS_ROM_data[10]),
    .OE_Addr(THE_DANGEROUS_ROM_data[7]), .CLK(debug_1_clk_out), .AAin(controlled_buffer_17_out),
    .AZin(controlled_buffer_16_out), .ABin(controlled_buffer_18_out),
    .DAin({REG_BANK_A_d_out_2, REG_BANK_A_d_out}), .DZin(controlled_buffer_2_out),
    .DBin({REG_BANK_B_d_out_2, REG_BANK_B_d_out}), .AAout(pull_resistor_3_node[9:5]), .AZout(OE_PC_out),
    .ABout(pull_resistor_3_node[4:0]), .Aout({REG_BANK_A_d_out_2, REG_BANK_A_d_out}),
    .Zout(controlled_buffer_2_out), .Bout({REG_BANK_B_d_out_2, REG_BANK_B_d_out}));
  Pull_Resistor pull_resistor_5 (.node(controlled_buffer_16_out));
  // RAM #(.addrWidth(5), .dataWidth(16), .databus("bidir"), .enables("line"), .\type ("nonvolatile")) RAM_INST: pin names not known; wires that end beside it: controlled_buffer_16_out, THE_DANGEROUS_ROM_data[60], THE_DANGEROUS_ROM_data[61], debug_1_clk_out, controlled_buffer_2_out
  // RAM #(.addrWidth(5), .dataWidth(16), .databus("bidir"), .enables("line"), .\type ("nonvolatile")) RAM_A: pin names not known; wires that end beside it: controlled_buffer_17_out, THE_DANGEROUS_ROM_data[58], THE_DANGEROUS_ROM_data[59], debug_1_clk_out, {REG_BANK_A_d_out_2, REG_BANK_A_d_out}
  // RAM #(.addrWidth(5), .dataWidth(16), .databus("bidir"), .enables("line"), .\type ("nonvolatile")) RAM_B: pin names not known; wires that end beside it: controlled_buffer_18_out, THE_DANGEROUS_ROM_data[56], THE_DANGEROUS_ROM_data[57], debug_1_clk_out, {REG_BANK_B_d_out_2, REG_BANK_B_d_out}
  // RAM #(.addrWidth(5), .dataWidth(16), .databus("bidir"), .enables("line"), .\type ("nonvolatile")) SYS_AREA: pin names not known; wires that end beside it: controlled_buffer_16_out, THE_DANGEROUS_ROM_data[54], THE_DANGEROUS_ROM_data[55], debug_1_clk_out, controlled_buffer_2_out

  // Notes on the sheet:
  //   contents of THE_DANGEROUS_ROM (hex, n*v repeats v):
  //   c000200000000000 1010100000000100 20800000000100 0 1 11*0 c000200000000000 1010100000000100
  //   20800000000100 4a0000000000 502054000000100 4009010000100 808110100 808050100 1 7*0 c000200000000000
  //   1010100000000100 20800000000100 400000000200 1 11*0 c000200000000000 1010100000000100 20800000000100
  //   4a0000000000 502054000000100 4009010000100 808110100 808050100 1 7*0 c000200000000000
  //   1010100000000100 20800000000100 480000000000 40000000800 10200000081180 88100000000100 1 8*0
  //   c000200000000000 1010100000000100 20800000000100 4a0000000000 502054000000100 1002000000900
  //   2004000002500 a01052000000100 1 7*0 c000200000000000 1010100000000100 20800000000100 2404000000120
  //   1002000000900 2004000002500 1402000000140 1 8*0 c000200000000000 1010100000000100 20800000000100
  //   400000000008 502004000000104 1003010000100 502004000000104 1002404000100 502004000000104
  //   1002101000100 502004000000104 1002040400100 1 0 0 0 c000200000000000 1010100000000100 20800000000100
  //   484008000100 42000000900 1088 10004002003500 88002000000904 10004000803500 88002000000904
  //   10004000203500 88002000000904 10000000003500 88000000000104 1 0 c000200000000000 1010100000000100
  //   20800000000100 808004100 202004100 80804100 20204100 10008100 4008100 1008100 408100 48100 1 0 0 0
  //   c000200000000000 1010100000000100 20800000000100 4a0000000000 502054000000100 4009010000100
  //   808110100 808050100 1 7*0 c000200000000000 1010100000000100 20800000000100 4a0000000000
  //   502054000000100 4009010000100 808110100 808050100 1 7*0 c000200000000000 1010100000000100
  //   20800000000100 4a0000000000 502054000000100 4009010000100 808110100 808050100 1 7*0 c000200000000000
  //   1010100000000100 20800000000100 4a0000000000 502054000000100 4009010000100 808110100 808050100 1 7*0
  //   c000200000000000 1010100000000100 20800000000100 0 1 11*0 c000200000000000 1010100000000100
  //   20800000000100 4a0000000000 10000000800 200000003080 50100000000100 8000000001900 2000000000500
  //   801040000000100 1 5*0 c000200000000000 1010100000000100 20800000000100 0 1 11*0 c000200000000000
  //   1010100000000100 20800000000100 4a0000000000 502054000000100 4009010000100 808110100 808050100 1 7*0
  //   c000200000000000 1010100000000100 20800000000100 0 1 11*0 c000200000000000 1010100000000100
  //   20800000000100 480000000000 40000000800 10200000021180 88100000000100 1 8*0 c000200000000000
  //   1010100000000100 20800000000100 0 1 11*0 c000200000000000 1010100000000100 20800000000100 0 1 11*0
  //   c000200000000000 1010100000000100 20800000000100 0 1 11*0 c000200000000000 1010100000000100
  //   20800000000100 0 1 11*0 c000200000000000 1010100000000100 20800000000100 0 1 11*0 c000200000000000
  //   1010100000000100 20800000000100 0 1 11*0 c000200000000000 1010100000000100 20800000000100 0 1 11*0
  //   c000200000000000 1010100000000100 20800000000100 0 1 11*0 c000200000000000 1010100000000100
  //   20800000000100 0 1 11*0 c000200000000000 1010100000000100 20800000000100 0 1 11*0 c000200000000000
  //   1010100000000100 20800000000100 2 1 11*0 c000200000000000 1010100000000100 20800000000100
  //   4a0000000000 50000000800 200000003080 50120000002180 8000000003900 4000000500 200012000000100 1
  //   Flag Bit
  //   OpCode
  //   Clock Counter
  //   Reset_SC
  //   OperandA (Addr1)
  //   HALT
  //   OE_AC
  //   WE_AC
  //   EN_DELAY
  //   DEBUG
  //   WE_TERM
  //   TERM_SEL_2
  //   TERM_SEL_1
  //   OE_ALU
  //   OE_OFL
  //   WE_OFL
  //   OE_O0
  //   WE_O0
  //   OE_B3
  //   WE_B3
  //   OE_B2
  //   WE_B2
  //   OE_B1
  //   WE_B1
  //   OE_B0
  //   WE_B0
  //   OE_A3
  //   WE_A3
  //   OE_A2
  //   WE_A2
  //   OE_A1
  //   WE_A1
  //   OE_A0
  //   WE_A0
  //   OE_MBR_B
  //   WE_MBR_B
  //   IOE_MBR_B
  //   OE_MAR_B
  //   WE_MAR_B
  //   OE_MAR_A
  //   WE_MAR_A
  //   OE_MAR
  //   WE_MAR
  //   OE_IR
  //   WE_IR
  //   OE_MBR_A
  //   WE_MBR_A
  //   IOE_MBR_A
  //   OE_MBR
  //   WE_MBR
  //   IOE_MBR
  //   OE_RAM_SYS
  //   OE_RAM_B
  //   WE_RAM_B
  //   OE_RAM_A
  //   WE_RAM_A
  //   OE_RAM_INST
  //   WE_RAM_INST
  //   OE_PC
  //   CE_PC
  //   OE_SWAP_REG
  //   WE_SWAP_REG
  //   OE_TERM_ADDR
  //   OE_TERM_DATA
  //   WE_MATMULT
  //   OE_MATMULT
  //   WE_RAM_SYS
  //   Addr2
  //   Addr1
  //   IDB_A
  //   IDB_B
  //   Logic for WEs:
  //   WE_MATMULT
  //   AND OE_Bs/OE_As
  //   Logic for R output:
  //   OE_MATMULT
  //   AND WE_B
  //   Int Address Bus
  //   Addr2
  //   Internal
  //   Data Bus
  //   Ext Address Bus
  //   EDB_A
  //   EDB_B
  //   External
  //   Data Bus
  //   O0=Reserved
  //   O1=ADD | SUB (F=1)
  //   O2=MUL
  //   O3=STO
  //   O4=STO OFL
  //   O5=SWAP MEM A TO B
  //   O6=SWAP REG
  //   O7=BLOCK LOAD
  //   O8=BLOCK STORE
  //   O9=MATMULT
  //   O10=CMP
  //   O11=AND
  //   O12=XOR
  //   O13=NOT
  //   O14=NOP | HALT (F=1)
  //   O15=NOP
  //   External Data Bus
endmodule

module BUS_TERM_ADDR (
  input  [4:0] AAin,
  input  [4:0] AZin,
  input  [4:0] ABin,
  input  [15:0] DAin,
  input  [15:0] DZin,
  input  [15:0] DBin,
  input  CLK,
  input  SELECT_1,
  input  SELECT_2,
  input  WE,
  input  OE_Data,
  input  OE_Addr,
  output [4:0] AAout,
  output [4:0] AZout,
  output [4:0] ABout,
  output [15:0] Aout,
  output [15:0] Zout,
  output [15:0] Bout
);

  wire controlled_buffer_14_out, controlled_buffer_16_out, DECODER_o1, DECODER_o2, DECODER_o3, DECODER_o4,
       not_1_out, not_2_out, pull_resistor_2_node, pull_resistor_4_node;
  wire [4:0] controlled_buffer_1_out, controlled_buffer_9_out, controlled_buffer_17_out,
       controlled_buffer_19_out, controlled_buffer_20_out, register_1_q, register_2_q;
  wire [15:0] controlled_buffer_4_out, controlled_buffer_11_out, controlled_buffer_18_out,
       controlled_buffer_22_out, controlled_buffer_23_out, TERM_A_q, TERM_B_q;

  DECODER_2x4 DECODER (.A({SELECT_2, SELECT_1}), .O1(DECODER_o1), .O2(DECODER_o2), .O3(DECODER_o3), .O4(DECODER_o4));
  assign controlled_buffer_1_out = DECODER_o2 ? ABin : 5'bz;  // Controlled_Buffer controlled_buffer_1
  assign controlled_buffer_1_out = DECODER_o3 ? AZin : 5'bz;  // Controlled_Buffer controlled_buffer_2
  assign controlled_buffer_1_out = DECODER_o1 ? AAin : 5'bz;  // Controlled_Buffer controlled_buffer_3
  assign controlled_buffer_4_out = DECODER_o2 ? DBin : 16'bz;  // Controlled_Buffer controlled_buffer_4
  assign controlled_buffer_4_out = DECODER_o3 ? DZin : 16'bz;  // Controlled_Buffer controlled_buffer_5
  assign controlled_buffer_4_out = DECODER_o1 ? DAin : 16'bz;  // Controlled_Buffer controlled_buffer_6
  Register #(.width(5)) register_1 (
    .D(controlled_buffer_1_out), .en(pull_resistor_2_node), .clk(CLK), .Q(register_1_q));  // open: clr
  Pull_Resistor pull_resistor_1 (.node(controlled_buffer_1_out));
  Pull_Resistor pull_resistor_2 (.node(pull_resistor_2_node));
  assign pull_resistor_2_node = not_1_out ? WE : 1'bz;  // Controlled_Buffer controlled_buffer_7
  Register #(.width(16)) TERM_A (
    .D(controlled_buffer_4_out), .en(pull_resistor_4_node), .clk(CLK), .Q(TERM_A_q));  // open: clr
  Pull_Resistor pull_resistor_3 (.node(controlled_buffer_4_out));
  Pull_Resistor pull_resistor_4 (.node(pull_resistor_4_node));
  assign pull_resistor_4_node = not_1_out ? WE : 1'bz;  // Controlled_Buffer controlled_buffer_8
  not not_1 (not_1_out, DECODER_o4);
  assign controlled_buffer_9_out = DECODER_o1 ? ABin : 5'bz;  // Controlled_Buffer controlled_buffer_9
  assign controlled_buffer_9_out = DECODER_o4 ? AZin : 5'bz;  // Controlled_Buffer controlled_buffer_10
  assign controlled_buffer_11_out = DECODER_o1 ? DBin : 16'bz;  // Controlled_Buffer controlled_buffer_11
  assign controlled_buffer_11_out = DECODER_o4 ? DZin : 16'bz;  // Controlled_Buffer controlled_buffer_12
  assign controlled_buffer_9_out = DECODER_o2 ? AAin : 5'bz;  // Controlled_Buffer controlled_buffer_13
  assign controlled_buffer_14_out = not_2_out ? WE : 1'bz;  // Controlled_Buffer controlled_buffer_14
  assign controlled_buffer_11_out = DECODER_o2 ? DAin : 16'bz;  // Controlled_Buffer controlled_buffer_15
  assign controlled_buffer_16_out = not_2_out ? WE : 1'bz;  // Controlled_Buffer controlled_buffer_16
  not not_2 (not_2_out, DECODER_o3);
  Pull_Resistor pull_resistor_5 (.node(controlled_buffer_14_out));
  Pull_Resistor pull_resistor_6 (.node(controlled_buffer_16_out));
  Register #(.width(5)) register_2 (
    .D(controlled_buffer_9_out), .en(controlled_buffer_14_out), .clk(CLK), .Q(register_2_q));  // open: clr
  Register #(.width(16)) TERM_B (
    .D(controlled_buffer_11_out), .en(controlled_buffer_16_out), .clk(CLK), .Q(TERM_B_q));  // open: clr
  assign controlled_buffer_17_out = DECODER_o2 ? register_1_q : 5'bz;  // Controlled_Buffer controlled_buffer_17
  assign controlled_buffer_18_out = DECODER_o2 ? TERM_A_q : 16'bz;  // Controlled_Buffer controlled_buffer_18
  assign controlled_buffer_19_out = DECODER_o3 ? register_1_q : 5'bz;  // Controlled_Buffer controlled_buffer_19
  assign controlled_buffer_20_out = DECODER_o1 ? register_1_q : 5'bz;  // Controlled_Buffer controlled_buffer_20
  assign controlled_buffer_17_out = DECODER_o1 ? register_2_q : 5'bz;  // Controlled_Buffer controlled_buffer_21
  assign controlled_buffer_22_out = DECODER_o3 ? TERM_A_q : 16'bz;  // Controlled_Buffer controlled_buffer_22
  assign controlled_buffer_23_out = DECODER_o1 ? TERM_A_q : 16'bz;  // Controlled_Buffer controlled_buffer_23
  assign controlled_buffer_18_out = DECODER_o1 ? TERM_B_q : 16'bz;  // Controlled_Buffer controlled_buffer_24
  assign controlled_buffer_19_out = DECODER_o4 ? register_2_q : 5'bz;  // Controlled_Buffer controlled_buffer_25
  assign controlled_buffer_20_out = DECODER_o2 ? register_2_q : 5'bz;  // Controlled_Buffer controlled_buffer_26
  assign Aout = OE_Data ? controlled_buffer_23_out : 16'bz;  // Controlled_Buffer controlled_buffer_27
  assign Zout = OE_Data ? controlled_buffer_22_out : 16'bz;  // Controlled_Buffer controlled_buffer_28
  assign Bout = OE_Data ? controlled_buffer_18_out : 16'bz;  // Controlled_Buffer controlled_buffer_29
  assign controlled_buffer_22_out = DECODER_o4 ? TERM_B_q : 16'bz;  // Controlled_Buffer controlled_buffer_30
  assign controlled_buffer_23_out = DECODER_o2 ? TERM_B_q : 16'bz;  // Controlled_Buffer controlled_buffer_31
  assign AAout = OE_Addr ? controlled_buffer_20_out : 5'bz;  // Controlled_Buffer controlled_buffer_32
  assign AZout = OE_Addr ? controlled_buffer_19_out : 5'bz;  // Controlled_Buffer controlled_buffer_33
  assign ABout = OE_Addr ? controlled_buffer_17_out : 5'bz;  // Controlled_Buffer controlled_buffer_34

  // Notes on the sheet:
  //   BS=10 Take middle as input: A takes Zin.
  //   BS=10 Output to middle: A outputs Zout
  //   BS=11 Take middle as input: B takes Zin.
  //   BS=11 Output to middle: B outputs Zout.
  //   SWAP REG: TERM_A outputs to Aout, TERM_B outputs to Bout
  //   BLOCK STORE: TERM_B takes input from Bin, outputs to Zout
  //   MOVE MEM: TERM_A takes input from Zin, outputs to Aout
  //   MOVE MEM: TERM_B takes input from Zin, outputs to Bout
  //   SWAP MEM: TERM_A takes input from Ain; TERM_B from Bin
  //   SWAP MEM: TERM_A outputs to Bout; TERM_B to Aout
  //   BS=00 Take normal input, A takes Ain; B takes Bin.
  //   BS=00 Normal Output; A outputs Aout; B outputs Bout
  //   BS=01 Take inverted inputs; A takes Bin; B takes Ain
  //   BS=01 Inverted Outputs: A outputs Bout; B outputs Aout
  //   SWAP REG: TERM_A takes input from Bin, and TERM_B takes input from Ain
endmodule

module DEBUG (
  input  [4:0] DELAY,
  input  WE,
  input  CLK,
  input  EN_DELAY,
  output CLK_OUT
);

  wire counter_1_carry, not_1_out, or_1_out, pull_resistor_3_node;
  wire [4:0] DELAY_REG_q;

  Register #(.width(5)) DELAY_REG (.D(DELAY), .en(WE), .clk(CLK), .Q(DELAY_REG_q), .clr(1'b0));
  Pull_Resistor pull_resistor_1 (.node(DELAY));
  Pull_Resistor pull_resistor_2 (.node(WE));
  Counter #(.max('h1f), .trigger("falling"), .width(5)) counter_1 (
    .load(or_1_out), .up(1'b0), .count(1'b1), .clk(CLK), .D(DELAY_REG_q), .carry(counter_1_carry));  // open: clr, Q
  or or_1 (or_1_out, counter_1_carry, not_1_out);
  Pull_Resistor pull_resistor_3 (.node(pull_resistor_3_node));
  assign pull_resistor_3_node = counter_1_carry ? CLK : 1'bz;  // Controlled_Buffer controlled_buffer_1
  not not_1 (not_1_out, EN_DELAY);
  Pull_Resistor pull_resistor_4 (.node(CLK_OUT));
  assign CLK_OUT = EN_DELAY ? pull_resistor_3_node : 1'bz;  // Controlled_Buffer controlled_buffer_2
  assign CLK_OUT = not_1_out ? CLK : 1'bz;  // Controlled_Buffer controlled_buffer_3
endmodule

module REG_SWAP_LOGIC (
  input  [4:0] AddrB,
  input  OE_B3,
  input  WE_B3,
  input  OE_B2,
  input  WE_B2,
  input  OE_B1,
  input  WE_B1,
  input  OE_B0,
  input  WE_B0,
  input  OE_A3,
  input  WE_A3,
  input  OE_A2,
  input  WE_A2,
  input  OE_A1,
  input  WE_A1,
  input  OE_A0,
  input  WE_A0,
  input  [4:0] AddrA,
  input  OE_SWAP_REG,
  input  WE_SWAP_REG,
  output out_21,
  output out_22,
  output out_23,
  output out_24,
  output out_25,
  output out_26,
  output out_27,
  output out_28,
  output out_29,
  output out_30,
  output out_31,
  output out_32,
  output out_33,
  output out_34,
  output out_35,
  output out_36
);

  wire controlled_buffer_1_out, controlled_buffer_2_out, controlled_buffer_3_out, controlled_buffer_4_out,
       controlled_buffer_5_out, controlled_buffer_6_out, controlled_buffer_7_out, controlled_buffer_8_out,
       controlled_buffer_9_out, controlled_buffer_10_out, controlled_buffer_11_out, controlled_buffer_12_out,
       controlled_buffer_13_out, controlled_buffer_14_out, controlled_buffer_15_out,
       controlled_buffer_16_out, decoder_2x4_1_o1, decoder_2x4_1_o2, decoder_2x4_1_o3, decoder_2x4_1_o4,
       decoder_2x4_2_o1, decoder_2x4_2_o2, decoder_2x4_2_o3, decoder_2x4_2_o4;

  DECODER_2x4 decoder_2x4_1 (
    .A(AddrB[1:0]), .O1(decoder_2x4_1_o1), .O2(decoder_2x4_1_o2), .O3(decoder_2x4_1_o3), .O4(decoder_2x4_1_o4));
  DECODER_2x4 decoder_2x4_2 (
    .A(AddrA[1:0]), .O1(decoder_2x4_2_o1), .O2(decoder_2x4_2_o2), .O3(decoder_2x4_2_o3), .O4(decoder_2x4_2_o4));
  assign controlled_buffer_1_out = OE_SWAP_REG ? decoder_2x4_1_o4 : 1'bz;  // Controlled_Buffer controlled_buffer_1
  assign controlled_buffer_2_out = WE_SWAP_REG ? decoder_2x4_1_o4 : 1'bz;  // Controlled_Buffer controlled_buffer_2
  assign controlled_buffer_3_out = OE_SWAP_REG ? decoder_2x4_1_o3 : 1'bz;  // Controlled_Buffer controlled_buffer_3
  assign controlled_buffer_4_out = WE_SWAP_REG ? decoder_2x4_1_o3 : 1'bz;  // Controlled_Buffer controlled_buffer_4
  assign controlled_buffer_5_out = OE_SWAP_REG ? decoder_2x4_1_o2 : 1'bz;  // Controlled_Buffer controlled_buffer_5
  assign controlled_buffer_6_out = WE_SWAP_REG ? decoder_2x4_1_o2 : 1'bz;  // Controlled_Buffer controlled_buffer_6
  assign controlled_buffer_7_out = OE_SWAP_REG ? decoder_2x4_1_o1 : 1'bz;  // Controlled_Buffer controlled_buffer_7
  assign controlled_buffer_8_out = WE_SWAP_REG ? decoder_2x4_1_o1 : 1'bz;  // Controlled_Buffer controlled_buffer_8
  assign controlled_buffer_9_out = OE_SWAP_REG ? decoder_2x4_2_o4 : 1'bz;  // Controlled_Buffer controlled_buffer_9
  assign controlled_buffer_10_out = WE_SWAP_REG ? decoder_2x4_2_o4 : 1'bz;  // Controlled_Buffer controlled_buffer_10
  assign controlled_buffer_11_out = OE_SWAP_REG ? decoder_2x4_2_o3 : 1'bz;  // Controlled_Buffer controlled_buffer_11
  assign controlled_buffer_12_out = WE_SWAP_REG ? decoder_2x4_2_o3 : 1'bz;  // Controlled_Buffer controlled_buffer_12
  assign controlled_buffer_13_out = OE_SWAP_REG ? decoder_2x4_2_o2 : 1'bz;  // Controlled_Buffer controlled_buffer_13
  assign controlled_buffer_14_out = WE_SWAP_REG ? decoder_2x4_2_o2 : 1'bz;  // Controlled_Buffer controlled_buffer_14
  assign controlled_buffer_15_out = OE_SWAP_REG ? decoder_2x4_2_o1 : 1'bz;  // Controlled_Buffer controlled_buffer_15
  assign controlled_buffer_16_out = WE_SWAP_REG ? decoder_2x4_2_o1 : 1'bz;  // Controlled_Buffer controlled_buffer_16
  Pull_Resistor pull_resistor_1 (.node(controlled_buffer_1_out));
  Pull_Resistor pull_resistor_2 (.node(controlled_buffer_2_out));
  Pull_Resistor pull_resistor_3 (.node(controlled_buffer_3_out));
  Pull_Resistor pull_resistor_4 (.node(controlled_buffer_4_out));
  Pull_Resistor pull_resistor_5 (.node(controlled_buffer_5_out));
  Pull_Resistor pull_resistor_6 (.node(controlled_buffer_6_out));
  Pull_Resistor pull_resistor_7 (.node(controlled_buffer_9_out));
  Pull_Resistor pull_resistor_8 (.node(controlled_buffer_10_out));
  Pull_Resistor pull_resistor_9 (.node(controlled_buffer_11_out));
  Pull_Resistor pull_resistor_10 (.node(controlled_buffer_12_out));
  Pull_Resistor pull_resistor_11 (.node(controlled_buffer_13_out));
  Pull_Resistor pull_resistor_12 (.node(controlled_buffer_14_out));
  Pull_Resistor pull_resistor_13 (.node(controlled_buffer_7_out));
  Pull_Resistor pull_resistor_14 (.node(controlled_buffer_8_out));
  Pull_Resistor pull_resistor_15 (.node(controlled_buffer_15_out));
  Pull_Resistor pull_resistor_16 (.node(controlled_buffer_16_out));
  or or_1 (out_21, OE_B3, controlled_buffer_1_out);
  or or_2 (out_22, WE_B3, controlled_buffer_2_out);
  or or_3 (out_23, OE_B2, controlled_buffer_3_out);
  or or_4 (out_24, WE_B2, controlled_buffer_4_out);
  or or_5 (out_25, OE_B1, controlled_buffer_5_out);
  or or_6 (out_26, WE_B1, controlled_buffer_6_out);
  or or_7 (out_27, OE_B0, controlled_buffer_7_out);
  or or_8 (out_28, WE_B0, controlled_buffer_8_out);
  or or_9 (out_29, OE_A3, controlled_buffer_9_out);
  or or_10 (out_30, WE_A3, controlled_buffer_10_out);
  or or_11 (out_31, OE_A2, controlled_buffer_11_out);
  or or_12 (out_32, WE_A2, controlled_buffer_12_out);
  or or_13 (out_33, OE_A1, controlled_buffer_13_out);
  or or_14 (out_34, WE_A1, controlled_buffer_14_out);
  or or_15 (out_35, OE_A0, controlled_buffer_15_out);
  or or_16 (out_36, WE_A0, controlled_buffer_16_out);
endmodule

module REG_SWAP_LOGIC_2 (
  input  [4:0] AddrB,
  input  OE_B3,
  input  WE_B3,
  input  OE_B2,
  input  WE_B2,
  input  OE_B1,
  input  WE_B1,
  input  OE_B0,
  input  WE_B0,
  input  OE_A3,
  input  WE_A3,
  input  OE_A2,
  input  WE_A2,
  input  OE_A1,
  input  WE_A1,
  input  OE_A0,
  input  WE_A0,
  input  [4:0] AddrA,
  input  OE_SWAP_REG,
  input  WE_SWAP_REG,
  output out_21,
  output out_22,
  output out_23,
  output out_24,
  output out_25,
  output out_26,
  output out_27,
  output out_28,
  output out_29,
  output out_30,
  output out_31,
  output out_32,
  output out_33,
  output out_34,
  output out_35,
  output out_36
);

  wire controlled_buffer_1_out, controlled_buffer_2_out, controlled_buffer_3_out, controlled_buffer_4_out,
       controlled_buffer_5_out, controlled_buffer_6_out, controlled_buffer_7_out, controlled_buffer_8_out,
       controlled_buffer_9_out, controlled_buffer_10_out, controlled_buffer_11_out, controlled_buffer_12_out,
       controlled_buffer_13_out, controlled_buffer_14_out, controlled_buffer_15_out,
       controlled_buffer_16_out, decoder_3x8_1_o2, decoder_3x8_1_o3, decoder_3x8_1_o4, decoder_3x8_1_o5,
       decoder_4x16_1_o5, decoder_4x16_1_o6, decoder_4x16_1_o7, decoder_4x16_1_o8;

  DECODER_4x16 decoder_4x16_1 (
    .in_1(AddrB[3:0]), .O5(decoder_4x16_1_o5), .O6(decoder_4x16_1_o6), .O7(decoder_4x16_1_o7),
    .O8(decoder_4x16_1_o8));  // open: O0, O1, O2, O3, O4, O9, O10, O11, O12, O13, O14, O15
  DECODER_3x8 decoder_3x8_1 (
    .A(AddrA[2:0]), .O2(decoder_3x8_1_o2), .O3(decoder_3x8_1_o3), .O4(decoder_3x8_1_o4), .O5(decoder_3x8_1_o5));  // open: O1, O6, O7, O8
  assign controlled_buffer_1_out = OE_SWAP_REG ? decoder_4x16_1_o8 : 1'bz;  // Controlled_Buffer controlled_buffer_1
  assign controlled_buffer_2_out = WE_SWAP_REG ? decoder_4x16_1_o8 : 1'bz;  // Controlled_Buffer controlled_buffer_2
  assign controlled_buffer_3_out = OE_SWAP_REG ? decoder_4x16_1_o7 : 1'bz;  // Controlled_Buffer controlled_buffer_3
  assign controlled_buffer_4_out = WE_SWAP_REG ? decoder_4x16_1_o7 : 1'bz;  // Controlled_Buffer controlled_buffer_4
  assign controlled_buffer_5_out = OE_SWAP_REG ? decoder_4x16_1_o6 : 1'bz;  // Controlled_Buffer controlled_buffer_5
  assign controlled_buffer_6_out = WE_SWAP_REG ? decoder_4x16_1_o6 : 1'bz;  // Controlled_Buffer controlled_buffer_6
  assign controlled_buffer_7_out = OE_SWAP_REG ? decoder_4x16_1_o5 : 1'bz;  // Controlled_Buffer controlled_buffer_7
  assign controlled_buffer_8_out = WE_SWAP_REG ? decoder_4x16_1_o5 : 1'bz;  // Controlled_Buffer controlled_buffer_8
  assign controlled_buffer_9_out = OE_SWAP_REG ? decoder_3x8_1_o5 : 1'bz;  // Controlled_Buffer controlled_buffer_9
  assign controlled_buffer_10_out = WE_SWAP_REG ? decoder_3x8_1_o5 : 1'bz;  // Controlled_Buffer controlled_buffer_10
  assign controlled_buffer_11_out = OE_SWAP_REG ? decoder_3x8_1_o4 : 1'bz;  // Controlled_Buffer controlled_buffer_11
  assign controlled_buffer_12_out = WE_SWAP_REG ? decoder_3x8_1_o4 : 1'bz;  // Controlled_Buffer controlled_buffer_12
  assign controlled_buffer_13_out = OE_SWAP_REG ? decoder_3x8_1_o3 : 1'bz;  // Controlled_Buffer controlled_buffer_13
  assign controlled_buffer_14_out = WE_SWAP_REG ? decoder_3x8_1_o3 : 1'bz;  // Controlled_Buffer controlled_buffer_14
  assign controlled_buffer_15_out = OE_SWAP_REG ? decoder_3x8_1_o2 : 1'bz;  // Controlled_Buffer controlled_buffer_15
  assign controlled_buffer_16_out = WE_SWAP_REG ? decoder_3x8_1_o2 : 1'bz;  // Controlled_Buffer controlled_buffer_16
  Pull_Resistor pull_resistor_1 (.node(controlled_buffer_1_out));
  Pull_Resistor pull_resistor_2 (.node(controlled_buffer_2_out));
  Pull_Resistor pull_resistor_3 (.node(controlled_buffer_3_out));
  Pull_Resistor pull_resistor_4 (.node(controlled_buffer_4_out));
  Pull_Resistor pull_resistor_5 (.node(controlled_buffer_5_out));
  Pull_Resistor pull_resistor_6 (.node(controlled_buffer_6_out));
  Pull_Resistor pull_resistor_7 (.node(controlled_buffer_9_out));
  Pull_Resistor pull_resistor_8 (.node(controlled_buffer_10_out));
  Pull_Resistor pull_resistor_9 (.node(controlled_buffer_11_out));
  Pull_Resistor pull_resistor_10 (.node(controlled_buffer_12_out));
  Pull_Resistor pull_resistor_11 (.node(controlled_buffer_13_out));
  Pull_Resistor pull_resistor_12 (.node(controlled_buffer_14_out));
  Pull_Resistor pull_resistor_13 (.node(controlled_buffer_7_out));
  Pull_Resistor pull_resistor_14 (.node(controlled_buffer_8_out));
  Pull_Resistor pull_resistor_15 (.node(controlled_buffer_15_out));
  Pull_Resistor pull_resistor_16 (.node(controlled_buffer_16_out));
  or or_1 (out_21, OE_B3, controlled_buffer_1_out);
  or or_2 (out_22, WE_B3, controlled_buffer_2_out);
  or or_3 (out_23, OE_B2, controlled_buffer_3_out);
  or or_4 (out_24, WE_B2, controlled_buffer_4_out);
  or or_5 (out_25, OE_B1, controlled_buffer_5_out);
  or or_6 (out_26, WE_B1, controlled_buffer_6_out);
  or or_7 (out_27, OE_B0, controlled_buffer_7_out);
  or or_8 (out_28, WE_B0, controlled_buffer_8_out);
  or or_9 (out_29, OE_A3, controlled_buffer_9_out);
  or or_10 (out_30, WE_A3, controlled_buffer_10_out);
  or or_11 (out_31, OE_A2, controlled_buffer_11_out);
  or or_12 (out_32, WE_A2, controlled_buffer_12_out);
  or or_13 (out_33, OE_A1, controlled_buffer_13_out);
  or or_14 (out_34, WE_A1, controlled_buffer_14_out);
  or or_15 (out_35, OE_A0, controlled_buffer_15_out);
  or or_16 (out_36, WE_A0, controlled_buffer_16_out);
endmodule

module ALU_16_bit (
  input  [15:0] A,
  input  [15:0] B,
  input  Flag_bit,
  input  [4:0] OpCode,
  input  OE,
  output [15:0] OFL,
  output [15:0] Rout,
  output [15:0] Result
);

  wire adder_16_bit_1_cout, adder_16_bit_1_ofl, and_1_out, controlled_buffer_1_out, decoder_5x32_1_o1,
       decoder_5x32_1_o3, decoder_5x32_1_o10, decoder_5x32_1_o11, decoder_5x32_1_o12, decoder_5x32_1_o13,
       not_3_out, NOT_A_out, NOT_B_out, pull_resistor_1_node, pull_resistor_2_node;
  wire [2:0] cmp_16_bit_1_lt, controlled_buffer_3_out;
  wire [15:0] adder_16_bit_1_s, and_2_out, bit_extender_1_out, mul_8_bit_1_product, mux_16_bit_1_o,
       mux_16_bit_2_o, not_1_out, not_2_out, or_1_out, pull_resistor_3_node, pull_resistor_4_node,
       pull_resistor_5_node, pull_resistor_6_node, pull_resistor_8_node, pull_resistor_9_node,
       pull_resistor_10_node, xor_1_out;

  // Probe on A
  // Probe on A
  assign not_1_out = ~A;  // NOT_Gate not_1, 16 bits wide
  // Probe on B
  // Probe on B
  assign not_2_out = ~B;  // NOT_Gate not_2, 16 bits wide
  // Probe on Result
  // Probe on Result
  MUX_16_bit mux_16_bit_1 (.S(NOT_A_out), .A(A), .B(not_1_out), .O(mux_16_bit_1_o));
  MUX_16_bit mux_16_bit_2 (.S(NOT_B_out), .A(B), .B(not_2_out), .O(mux_16_bit_2_o));
  // Probe on mux_16_bit_2_o
  Pull_Resistor pull_resistor_1 (.node(pull_resistor_1_node));
  DECODER_5x32 decoder_5x32_1 (
    .in_1(OpCode), .O1(decoder_5x32_1_o1), .O3(decoder_5x32_1_o3), .O10(decoder_5x32_1_o10),
    .O11(decoder_5x32_1_o11), .O12(decoder_5x32_1_o12), .O13(decoder_5x32_1_o13));  // open: O0, O2, O4, O5, O6, O7, O8, O9, O14, O15, O16, O17, O18, O19, O20, O21, O22, O23, O24, O25, O26, O27, O28, O29, O30, O31
  or NOT_A (NOT_A_out, pull_resistor_1_node, decoder_5x32_1_o13);
  Pull_Resistor pull_resistor_2 (.node(pull_resistor_2_node));
  or NOT_B (NOT_B_out, pull_resistor_2_node, and_1_out);
  and and_1 (and_1_out, Flag_bit, decoder_5x32_1_o1);
  assign or_1_out = mux_16_bit_1_o | mux_16_bit_2_o;  // OR_Gate or_1, 16 bits wide
  assign and_2_out = mux_16_bit_1_o & mux_16_bit_2_o;  // AND_Gate and_2, 16 bits wide
  assign xor_1_out = mux_16_bit_1_o ^ mux_16_bit_2_o;  // XOR_Gate xor_1, 16 bits wide
  ADDER_16_bit adder_16_bit_1 (
    .B(mux_16_bit_2_o), .A(mux_16_bit_1_o), .Cin(and_1_out), .Cout(adder_16_bit_1_cout),
    .OFL(adder_16_bit_1_ofl), .S(adder_16_bit_1_s));
  assign controlled_buffer_1_out = decoder_5x32_1_o1 ? adder_16_bit_1_cout : 1'bz;  // Controlled_Buffer controlled_buffer_1
  assign controlled_buffer_3_out[2] = decoder_5x32_1_o1 ? adder_16_bit_1_ofl : 1'bz;  // Controlled_Buffer controlled_buffer_2
  CMP_16_bit cmp_16_bit_1 (
    .A(mux_16_bit_1_o), .B(mux_16_bit_2_o), .GT(cmp_16_bit_1_lt[2]), .LT(cmp_16_bit_1_lt[0]),
    .EQ(cmp_16_bit_1_lt[1]));
  MUL_8_bit mul_8_bit_1 (.A(mux_16_bit_1_o[7:0]), .B(mux_16_bit_2_o[7:0]), .Product(mul_8_bit_1_product));
  // Probe on or_1_out
  not not_3 (not_3_out, and_1_out);
  assign controlled_buffer_3_out[0] = not_3_out ? controlled_buffer_1_out : 1'bz;  // Controlled_Buffer controlled_buffer_3
  assign bit_extender_1_out = {{13{1'b0}}, cmp_16_bit_1_lt};  // Bit_Extender bit_extender_1
  Pull_Resistor pull_resistor_3 (.node(pull_resistor_3_node));
  Controlled_Buffer #(.width(16)) controlled_buffer_4 (.in(or_1_out), .out(pull_resistor_3_node));  // open: en
  Pull_Resistor pull_resistor_4 (.node(pull_resistor_4_node));
  assign pull_resistor_4_node = decoder_5x32_1_o11 ? and_2_out : 16'bz;  // Controlled_Buffer controlled_buffer_5
  Pull_Resistor pull_resistor_5 (.node(pull_resistor_5_node));
  assign pull_resistor_5_node = decoder_5x32_1_o12 ? xor_1_out : 16'bz;  // Controlled_Buffer controlled_buffer_6
  Pull_Resistor pull_resistor_6 (.node(pull_resistor_6_node));
  assign pull_resistor_6_node = decoder_5x32_1_o1 ? adder_16_bit_1_s : 16'bz;  // Controlled_Buffer controlled_buffer_7
  Pull_Resistor pull_resistor_7 (.node(controlled_buffer_3_out[2]));
  Pull_Resistor pull_resistor_8 (.node(pull_resistor_8_node));
  assign pull_resistor_8_node = decoder_5x32_1_o10 ? bit_extender_1_out : 16'bz;  // Controlled_Buffer controlled_buffer_8
  Pull_Resistor pull_resistor_9 (.node(pull_resistor_9_node));
  assign pull_resistor_9_node = decoder_5x32_1_o13 ? mux_16_bit_1_o : 16'bz;  // Controlled_Buffer controlled_buffer_9
  Pull_Resistor pull_resistor_10 (.node(pull_resistor_10_node));
  assign pull_resistor_10_node = decoder_5x32_1_o3 ? mul_8_bit_1_product : 16'bz;  // Controlled_Buffer controlled_buffer_10
  Pull_Resistor pull_resistor_11 (.node(controlled_buffer_3_out[0]));
  assign OFL = OE ? {{13{1'b0}}, controlled_buffer_3_out[2], 1'b0, controlled_buffer_3_out[0]} : 16'bz;  // Controlled_Buffer controlled_buffer_11
  assign Result = pull_resistor_3_node | pull_resistor_4_node | pull_resistor_5_node | pull_resistor_6_node | pull_resistor_8_node | pull_resistor_9_node | pull_resistor_10_node;  // OR_Gate or_2, 16 bits wide
  assign Rout = OE ? Result : 16'bz;  // Controlled_Buffer controlled_buffer_12

  // Notes on the sheet:
  //   O0=Reserved
  //   O1=ADD | SUB (F=1)
  //   O2=MUL
  //   O3=STO
  //   O4=STO OFL
  //   O5=SWAP MEM A TO B
  //   O6=SWAP REG
  //   O7=BLOCK LOAD
  //   O8=BLOCK STORE
  //   O9=MATMULT
  //   O10=CMP
  //   O11=AND
  //   O12=XOR
  //   O13=NOT
  //   O14=NOP | HALT (F=1)
  //   O15=NOP
endmodule

module MUL_8_bit (
  input  [7:0] A,
  input  [7:0] B,
  output [15:0] Product
);

  wire [3:0] undriven_2, undriven_3, undriven_4, undriven_5;
  wire [7:0] mul_4_bit_1_product, mul_4_bit_2_product, mul_4_bit_3_product, mul_4_bit_4_product, undriven,
       undriven_6;
  wire [15:0] adder_16_bit_1_s, adder_16_bit_2_s;

  MUL_4_bit mul_4_bit_1 (.A(A[3:0]), .B(B[3:0]), .Product(mul_4_bit_1_product));
  MUL_4_bit mul_4_bit_2 (.A(A[3:0]), .B(B[7:4]), .Product(mul_4_bit_2_product));
  MUL_4_bit mul_4_bit_3 (.A(A[7:4]), .B(B[3:0]), .Product(mul_4_bit_3_product));
  MUL_4_bit mul_4_bit_4 (.A(A[7:4]), .B(B[7:4]), .Product(mul_4_bit_4_product));
  ADDER_16_bit adder_16_bit_1 (
    .B({undriven_3, mul_4_bit_2_product, undriven_2}), .A({undriven, mul_4_bit_1_product}),
    .S(adder_16_bit_1_s));  // open: Cin, Cout, OFL
  ADDER_16_bit adder_16_bit_2 (
    .B({mul_4_bit_4_product, undriven_6}), .A({undriven_5, mul_4_bit_3_product, undriven_4}),
    .S(adder_16_bit_2_s));  // open: Cin, Cout, OFL
  ADDER_16_bit adder_16_bit_3 (.B(adder_16_bit_2_s), .A(adder_16_bit_1_s), .S(Product));  // open: Cin, Cout, OFL
endmodule

module ADDER_16_bit (
  input  Cin,
  input  [15:0] A,
  input  [15:0] B,
  output [15:0] S,
  output OFL,
  output Cout
);

  wire adder_1bit_1_cout, adder_1bit_2_cout, adder_1bit_3_cout, adder_1bit_4_cout, adder_1bit_5_cout,
       adder_1bit_6_cout, adder_1bit_7_cout, adder_1bit_8_cout, adder_1bit_9_cout, adder_1bit_10_cout,
       adder_1bit_11_cout, adder_1bit_12_cout, adder_1bit_13_cout, adder_1bit_14_cout, adder_1bit_15_cout;

  // Probe on A
  // Probe on B
  // Probe on S
  // Probe on S
  ADDER_1bit adder_1bit_1 (.A(A[0]), .B(B[0]), .Cin(Cin), .S(S[0]), .Cout(adder_1bit_1_cout));
  ADDER_1bit adder_1bit_2 (.A(A[1]), .B(B[1]), .Cin(adder_1bit_1_cout), .S(S[1]), .Cout(adder_1bit_2_cout));
  ADDER_1bit adder_1bit_3 (.A(A[2]), .B(B[2]), .Cin(adder_1bit_2_cout), .S(S[2]), .Cout(adder_1bit_3_cout));
  ADDER_1bit adder_1bit_4 (.A(A[3]), .B(B[3]), .Cin(adder_1bit_3_cout), .S(S[3]), .Cout(adder_1bit_4_cout));
  ADDER_1bit adder_1bit_5 (.A(A[4]), .B(B[4]), .Cin(adder_1bit_4_cout), .S(S[4]), .Cout(adder_1bit_5_cout));
  ADDER_1bit adder_1bit_6 (.A(A[5]), .B(B[5]), .Cin(adder_1bit_5_cout), .S(S[5]), .Cout(adder_1bit_6_cout));
  ADDER_1bit adder_1bit_7 (.A(A[6]), .B(B[6]), .Cin(adder_1bit_6_cout), .S(S[6]), .Cout(adder_1bit_7_cout));
  ADDER_1bit adder_1bit_8 (.A(A[7]), .B(B[7]), .Cin(adder_1bit_7_cout), .S(S[7]), .Cout(adder_1bit_8_cout));
  ADDER_1bit adder_1bit_9 (.A(A[8]), .B(B[8]), .Cin(adder_1bit_8_cout), .S(S[8]), .Cout(adder_1bit_9_cout));
  ADDER_1bit adder_1bit_10 (.A(A[9]), .B(B[9]), .Cin(adder_1bit_9_cout), .S(S[9]), .Cout(adder_1bit_10_cout));
  ADDER_1bit adder_1bit_11 (.A(A[10]), .B(B[10]), .Cin(adder_1bit_10_cout), .S(S[10]), .Cout(adder_1bit_11_cout));
  ADDER_1bit adder_1bit_12 (.A(A[11]), .B(B[11]), .Cin(adder_1bit_11_cout), .S(S[11]), .Cout(adder_1bit_12_cout));
  ADDER_1bit adder_1bit_13 (.A(A[12]), .B(B[12]), .Cin(adder_1bit_12_cout), .S(S[12]), .Cout(adder_1bit_13_cout));
  ADDER_1bit adder_1bit_14 (.A(A[13]), .B(B[13]), .Cin(adder_1bit_13_cout), .S(S[13]), .Cout(adder_1bit_14_cout));
  ADDER_1bit adder_1bit_15 (.A(A[14]), .B(B[14]), .Cin(adder_1bit_14_cout), .S(S[14]), .Cout(adder_1bit_15_cout));
  ADDER_1bit adder_1bit_16 (.A(A[15]), .B(B[15]), .Cin(adder_1bit_15_cout), .S(S[15]), .Cout(Cout));
  xor xor_1 (OFL, adder_1bit_15_cout, Cout);
endmodule

module MUX_16_bit (
  input  S,
  input  [15:0] A,
  input  [15:0] B,
  output [15:0] O
);

  wire [15:0] and_1_out, and_2_out, bit_extender_1_out, not_1_out;

  assign bit_extender_1_out = {{15{S}}, S};  // Bit_Extender bit_extender_1
  assign not_1_out = ~bit_extender_1_out;  // NOT_Gate not_1, 16 bits wide
  assign and_1_out = A & not_1_out;  // AND_Gate and_1, 16 bits wide
  assign and_2_out = bit_extender_1_out & B;  // AND_Gate and_2, 16 bits wide
  assign O = and_1_out | and_2_out;  // OR_Gate or_1, 16 bits wide

  // Notes on the sheet:
  //   A: pull=up
endmodule

module CMP_16_bit (
  input  [15:0] A,
  input  [15:0] B,
  output GT,
  output LT,
  output EQ
);

  wire and_1_out, and_2_out, cmp_8_bit_1_eq, cmp_8_bit_1_gt, cmp_8_bit_1_lt, cmp_8_bit_2_eq, cmp_8_bit_2_gt,
       cmp_8_bit_2_lt;

  CMP_8_bit cmp_8_bit_1 (.A(A[7:0]), .B(B[7:0]), .GT(cmp_8_bit_1_gt), .EQ(cmp_8_bit_1_eq), .LT(cmp_8_bit_1_lt));
  CMP_8_bit cmp_8_bit_2 (.A(A[15:8]), .B(B[15:8]), .GT(cmp_8_bit_2_gt), .EQ(cmp_8_bit_2_eq), .LT(cmp_8_bit_2_lt));
  and and_1 (and_1_out, cmp_8_bit_1_gt, cmp_8_bit_2_eq);
  and and_2 (and_2_out, cmp_8_bit_1_lt, cmp_8_bit_2_eq);
  or or_1 (GT, and_1_out, cmp_8_bit_2_gt);
  and and_3 (EQ, cmp_8_bit_1_eq, cmp_8_bit_2_eq);
  or or_2 (LT, and_2_out, cmp_8_bit_2_lt);
endmodule

module REG_BANK (
  input  CLK,
  input  [15:0] D_in,
  input  WE_0,
  input  OE_0,
  input  WE_1,
  input  OE_1,
  input  WE_2,
  input  OE_2,
  input  WE_3,
  input  OE_3,
  output [15:0] D_out
);

  wire [15:0] register_1_q, register_2_q, register_3_q, register_4_q;

  Register #(.width(16)) register_1 (.D(D_in), .en(WE_0), .clk(CLK), .Q(register_1_q));  // open: clr
  Register #(.width(16)) register_2 (.D(D_in), .en(WE_1), .clk(CLK), .Q(register_2_q));  // open: clr
  Register #(.width(16)) register_3 (.D(D_in), .en(WE_2), .clk(CLK), .Q(register_3_q));  // open: clr
  Register #(.width(16)) register_4 (.D(D_in), .en(WE_3), .clk(CLK), .Q(register_4_q));  // open: clr
  assign D_out = OE_0 ? register_1_q : 16'bz;  // Controlled_Buffer controlled_buffer_1
  assign D_out = OE_1 ? register_2_q : 16'bz;  // Controlled_Buffer controlled_buffer_2
  assign D_out = OE_2 ? register_3_q : 16'bz;  // Controlled_Buffer controlled_buffer_3
  assign D_out = OE_3 ? register_4_q : 16'bz;  // Controlled_Buffer controlled_buffer_4
endmodule

module MATMULT8 (
  input  CLK,
  input  [7:0] D_A,
  input  [7:0] D_B,
  input  OE,
  input  WE_A,
  input  WE_B,
  input  WE_C,
  input  WE_D,
  input  WE_E,
  input  WE_F,
  input  WE_G,
  input  WE_H,
  input  WE,
  output [15:0] R1,
  output [15:0] R2,
  output [15:0] R3,
  output [15:0] R4,
  output [15:0] OFL
);

  wire controlled_buffer_1_out, controlled_buffer_2_out, controlled_buffer_3_out, controlled_buffer_4_out,
       pull_resistor_2_node, pull_resistor_3_node, pull_resistor_4_node, pull_resistor_5_node;
  wire [6:0] adder_16_bit_1_cout;
  wire [7:0] register_1_q, register_2_q, register_3_q, register_4_q, register_5_q, register_6_q,
       register_7_q, register_8_q;
  wire [15:0] adder_16_bit_1_s, adder_16_bit_2_s, adder_16_bit_3_s, adder_16_bit_4_s, AxE_product,
       AxF_product, BxG_product, BxH_product, CxE_product, CxF_product, DxG_product, DxH_product;

  Pull_Resistor pull_resistor_1 (.node(D_B));
  assign controlled_buffer_1_out = WE ? WE_A : 1'bz;  // Controlled_Buffer controlled_buffer_1
  assign controlled_buffer_2_out = WE ? WE_B : 1'bz;  // Controlled_Buffer controlled_buffer_2
  assign controlled_buffer_3_out = WE ? WE_C : 1'bz;  // Controlled_Buffer controlled_buffer_3
  assign controlled_buffer_4_out = WE ? WE_D : 1'bz;  // Controlled_Buffer controlled_buffer_4
  Pull_Resistor pull_resistor_2 (.node(pull_resistor_2_node));
  assign pull_resistor_2_node = WE ? WE_E : 1'bz;  // Controlled_Buffer controlled_buffer_5
  Pull_Resistor pull_resistor_3 (.node(pull_resistor_3_node));
  assign pull_resistor_3_node = WE ? WE_F : 1'bz;  // Controlled_Buffer controlled_buffer_6
  Pull_Resistor pull_resistor_4 (.node(pull_resistor_4_node));
  assign pull_resistor_4_node = WE ? WE_G : 1'bz;  // Controlled_Buffer controlled_buffer_7
  Pull_Resistor pull_resistor_5 (.node(pull_resistor_5_node));
  assign pull_resistor_5_node = WE ? WE_H : 1'bz;  // Controlled_Buffer controlled_buffer_8
  Pull_Resistor pull_resistor_6 (.node(D_A));
  Pull_Resistor pull_resistor_7 (.node(CLK));
  Pull_Resistor pull_resistor_8 (.node(controlled_buffer_1_out));
  Pull_Resistor pull_resistor_9 (.node(controlled_buffer_2_out));
  Pull_Resistor pull_resistor_10 (.node(controlled_buffer_3_out));
  Pull_Resistor pull_resistor_11 (.node(controlled_buffer_4_out));
  Register register_1 (.D(D_A), .en(controlled_buffer_1_out), .clk(CLK), .Q(register_1_q));  // open: clr
  Register register_2 (.D(D_A), .en(controlled_buffer_2_out), .clk(CLK), .Q(register_2_q));  // open: clr
  Register register_3 (.D(D_A), .en(controlled_buffer_3_out), .clk(CLK), .Q(register_3_q));  // open: clr
  Register register_4 (.D(D_A), .en(controlled_buffer_4_out), .clk(CLK), .Q(register_4_q));  // open: clr
  Register register_5 (.D(D_B), .en(pull_resistor_2_node), .clk(CLK), .Q(register_5_q));  // open: clr
  Register register_6 (.D(D_B), .en(pull_resistor_3_node), .clk(CLK), .Q(register_6_q));  // open: clr
  Register register_7 (.D(D_B), .en(pull_resistor_4_node), .clk(CLK), .Q(register_7_q));  // open: clr
  Register register_8 (.D(D_B), .en(pull_resistor_5_node), .clk(CLK), .Q(register_8_q));  // open: clr
  MUL_8_bit AxE (.A(register_1_q), .B(register_5_q), .Product(AxE_product));
  MUL_8_bit BxG (.A(register_2_q), .B(register_7_q), .Product(BxG_product));
  MUL_8_bit AxF (.A(register_1_q), .B(register_6_q), .Product(AxF_product));
  MUL_8_bit BxH (.A(register_2_q), .B(register_8_q), .Product(BxH_product));
  MUL_8_bit CxE (.A(register_3_q), .B(register_5_q), .Product(CxE_product));
  MUL_8_bit DxG (.A(register_4_q), .B(register_7_q), .Product(DxG_product));
  MUL_8_bit CxF (.A(register_3_q), .B(register_6_q), .Product(CxF_product));
  MUL_8_bit DxH (.A(register_4_q), .B(register_8_q), .Product(DxH_product));
  ADDER_16_bit adder_16_bit_1 (
    .B(BxG_product), .A(AxE_product), .Cin(1'b0), .Cout(adder_16_bit_1_cout[0]), .S(adder_16_bit_1_s));  // open: OFL
  ADDER_16_bit adder_16_bit_2 (
    .B(BxH_product), .A(AxF_product), .Cin(1'b0), .Cout(adder_16_bit_1_cout[2]), .S(adder_16_bit_2_s));  // open: OFL
  ADDER_16_bit adder_16_bit_3 (
    .B(DxG_product), .A(CxE_product), .Cin(1'b0), .Cout(adder_16_bit_1_cout[4]), .S(adder_16_bit_3_s));  // open: OFL
  ADDER_16_bit adder_16_bit_4 (
    .B(DxH_product), .A(CxF_product), .Cin(1'b0), .Cout(adder_16_bit_1_cout[6]), .S(adder_16_bit_4_s));  // open: OFL
  assign R1 = OE ? adder_16_bit_1_s : 16'bz;  // Controlled_Buffer controlled_buffer_9
  assign R2 = OE ? adder_16_bit_2_s : 16'bz;  // Controlled_Buffer controlled_buffer_10
  assign R3 = OE ? adder_16_bit_3_s : 16'bz;  // Controlled_Buffer controlled_buffer_11
  assign R4 = OE ? adder_16_bit_4_s : 16'bz;  // Controlled_Buffer controlled_buffer_12
  assign OFL = OE ? {{9{1'b0}}, adder_16_bit_1_cout[6], 1'b0, adder_16_bit_1_cout[4], 1'b0, adder_16_bit_1_cout[2], 1'b0, adder_16_bit_1_cout[0]} : 16'bz;  // Controlled_Buffer controlled_buffer_13

  // Notes on the sheet:
  //   a b
  //   [
  //   ]
  //   x
  //   c d
  //   e f
  //   [
  //   g h
  //   ]
  //   =
  //   a.e + b.g   a.f + b.h
  //   [
  //   c.e + d.g   c.f + d.h
  //   ]
endmodule

module DECODER_2x4 (
  input  [1:0] A,
  output O1,
  output O2,
  output O3,
  output O4
);

  wire not_1_out, not_2_out;

  not not_1 (not_1_out, A[0]);
  not not_2 (not_2_out, A[1]);
  and and_1 (O1, not_2_out, not_1_out);
  and and_2 (O2, not_2_out, A[0]);
  and and_3 (O3, not_1_out, A[1]);
  and and_4 (O4, A[0], A[1]);
endmodule

module DECODER_3x8 (
  input  [2:0] A,
  output O1,
  output O2,
  output O3,
  output O4,
  output O5,
  output O6,
  output O7,
  output O8
);

  wire not_1_out, not_2_out, not_3_out;

  not not_1 (not_1_out, A[0]);
  not not_2 (not_2_out, A[1]);
  not not_3 (not_3_out, A[2]);
  and and_1 (O1, not_3_out, not_2_out, not_1_out);
  and and_2 (O2, not_3_out, not_2_out, A[0]);
  and and_3 (O3, not_3_out, A[1], not_1_out);
  and and_4 (O4, not_3_out, A[1], A[0]);
  and and_5 (O5, A[2], not_2_out, not_1_out);
  and and_6 (O6, A[2], not_2_out, A[0]);
  and and_7 (O7, A[2], A[1], not_1_out);
  and and_8 (O8, A[2], A[1], A[0]);
endmodule

module DECODER_4x16 (
  input  [3:0] in_1,
  output O0,
  output O1,
  output O2,
  output O3,
  output O4,
  output O5,
  output O6,
  output O7,
  output O8,
  output O9,
  output O10,
  output O11,
  output O12,
  output O13,
  output O14,
  output O15
);

  wire not_1_out, not_2_out, not_3_out, not_4_out;

  not not_1 (not_1_out, in_1[0]);
  not not_2 (not_2_out, in_1[1]);
  not not_3 (not_3_out, in_1[2]);
  not not_4 (not_4_out, in_1[3]);
  and and_1 (O0, not_4_out, not_3_out, not_2_out, not_1_out);
  and and_2 (O1, not_4_out, not_3_out, not_2_out, in_1[0]);
  and and_3 (O2, not_4_out, not_3_out, in_1[1], not_1_out);
  and and_4 (O3, not_4_out, not_3_out, in_1[1], in_1[0]);
  and and_5 (O4, not_4_out, in_1[2], not_2_out, not_1_out);
  and and_6 (O5, not_4_out, in_1[2], not_2_out, in_1[0]);
  and and_7 (O6, not_4_out, in_1[2], in_1[1], not_1_out);
  and and_8 (O7, not_4_out, in_1[2], in_1[1], in_1[0]);
  and and_9 (O8, in_1[3], not_3_out, not_2_out, not_1_out);
  and and_10 (O9, in_1[3], not_3_out, not_2_out, in_1[0]);
  and and_11 (O10, in_1[3], not_3_out, in_1[1], not_1_out);
  and and_12 (O11, in_1[3], not_3_out, in_1[1], in_1[0]);
  and and_13 (O12, in_1[3], in_1[2], not_2_out, not_1_out);
  and and_14 (O13, in_1[3], in_1[2], not_2_out, in_1[0]);
  and and_15 (O14, in_1[3], in_1[2], in_1[1], not_1_out);
  and and_16 (O15, in_1[3], in_1[2], in_1[1], in_1[0]);
endmodule

module DECODER_5x32 (
  input  [4:0] in_1,
  output O0,
  output O1,
  output O2,
  output O3,
  output O4,
  output O5,
  output O6,
  output O7,
  output O8,
  output O9,
  output O10,
  output O11,
  output O12,
  output O13,
  output O14,
  output O15,
  output O16,
  output O17,
  output O18,
  output O19,
  output O20,
  output O21,
  output O22,
  output O23,
  output O24,
  output O25,
  output O26,
  output O27,
  output O28,
  output O29,
  output O30,
  output O31
);

  wire not_1_out, not_2_out, not_3_out, not_4_out, not_5_out;

  not not_1 (not_1_out, in_1[4]);
  not not_2 (not_2_out, in_1[3]);
  not not_3 (not_3_out, in_1[2]);
  not not_4 (not_4_out, in_1[1]);
  not not_5 (not_5_out, in_1[0]);
  and and_1 (O0, not_5_out, not_4_out, not_3_out, not_2_out, not_1_out);
  and and_2 (O1, in_1[0], not_4_out, not_3_out, not_2_out, not_1_out);
  and and_3 (O2, not_5_out, in_1[1], not_3_out, not_2_out, not_1_out);
  and and_4 (O3, in_1[0], in_1[1], not_3_out, not_2_out, not_1_out);
  and and_5 (O4, not_5_out, not_4_out, in_1[2], not_2_out, not_1_out);
  and and_6 (O5, in_1[0], not_4_out, in_1[2], not_2_out, not_1_out);
  and and_7 (O6, not_5_out, in_1[1], in_1[2], not_2_out, not_1_out);
  and and_8 (O7, in_1[0], in_1[1], in_1[2], not_2_out, not_1_out);
  and and_9 (O8, not_5_out, not_4_out, not_3_out, in_1[3], not_1_out);
  and and_10 (O9, in_1[0], not_4_out, not_3_out, in_1[3], not_1_out);
  and and_11 (O10, not_5_out, in_1[1], not_3_out, in_1[3], not_1_out);
  and and_12 (O11, in_1[0], in_1[1], not_3_out, in_1[3], not_1_out);
  and and_13 (O12, not_5_out, not_4_out, in_1[2], in_1[3], not_1_out);
  and and_14 (O13, in_1[0], not_4_out, in_1[2], in_1[3], not_1_out);
  and and_15 (O14, not_5_out, in_1[1], in_1[2], in_1[3], not_1_out);
  and and_16 (O15, in_1[0], in_1[1], in_1[2], in_1[3], not_1_out);
  and and_17 (O16, not_5_out, not_4_out, not_3_out, not_2_out, in_1[4]);
  and and_18 (O17, in_1[0], not_4_out, not_3_out, not_2_out, in_1[4]);
  and and_19 (O18, not_5_out, in_1[1], not_3_out, not_2_out, in_1[4]);
  and and_20 (O19, in_1[0], in_1[1], not_3_out, not_2_out, in_1[4]);
  and and_21 (O20, not_5_out, not_4_out, in_1[2], not_2_out, in_1[4]);
  and and_22 (O21, in_1[0], not_4_out, in_1[2], not_2_out, in_1[4]);
  and and_23 (O22, not_5_out, in_1[1], in_1[2], not_2_out, in_1[4]);
  and and_24 (O23, in_1[0], in_1[1], in_1[2], not_2_out, in_1[4]);
  and and_25 (O24, not_5_out, not_4_out, not_3_out, in_1[3], in_1[4]);
  and and_26 (O25, in_1[0], not_4_out, not_3_out, in_1[3], in_1[4]);
  and and_27 (O26, not_5_out, in_1[1], not_3_out, in_1[3], in_1[4]);
  and and_28 (O27, in_1[0], in_1[1], not_3_out, in_1[3], in_1[4]);
  and and_29 (O28, not_5_out, not_4_out, in_1[2], in_1[3], in_1[4]);
  and and_30 (O29, in_1[0], not_4_out, in_1[2], in_1[3], in_1[4]);
  and and_31 (O30, not_5_out, in_1[1], in_1[2], in_1[3], in_1[4]);
  and and_32 (O31, in_1[0], in_1[1], in_1[2], in_1[3], in_1[4]);
endmodule

module MUL_4_bit (
  input  [3:0] A,
  input  [3:0] B,
  output [7:0] Product
);

  wire [2:0] and_15_out;
  wire [3:0] adder_4_bit_2_cout, adder_4_bit_3_cout, and_4_out, and_8_out, and_12_out;

  and and_1 (and_4_out[3], A[3], B[3]);
  and and_2 (and_4_out[2], A[3], B[2]);
  and and_3 (and_4_out[1], A[3], B[1]);
  and and_4 (and_4_out[0], A[3], B[0]);
  and and_5 (and_8_out[3], A[2], B[3]);
  and and_6 (and_8_out[2], A[2], B[2]);
  and and_7 (and_8_out[1], A[2], B[1]);
  and and_8 (and_8_out[0], A[2], B[0]);
  and and_9 (and_12_out[3], A[1], B[3]);
  and and_10 (and_12_out[2], A[1], B[2]);
  and and_11 (and_12_out[1], A[1], B[1]);
  ADDER_4_bit adder_4_bit_1 (.Cin(1'b0), .A(adder_4_bit_2_cout), .B(and_4_out), .Cout(Product[7]), .S(Product[6:3]));
  and and_12 (and_12_out[0], A[1], B[0]);
  ADDER_4_bit adder_4_bit_2 (
    .Cin(1'b0), .A(adder_4_bit_3_cout), .B(and_8_out), .Cout(adder_4_bit_2_cout[3]),
    .S({adder_4_bit_2_cout[2:0], Product[2]}));
  and and_13 (and_15_out[1], A[0], B[2]);
  and and_14 (and_15_out[2], A[0], B[3]);
  ADDER_4_bit adder_4_bit_3 (
    .Cin(1'b0), .A({1'b0, and_15_out}), .B(and_12_out), .Cout(adder_4_bit_3_cout[3]),
    .S({adder_4_bit_3_cout[2:0], Product[1]}));
  and and_15 (and_15_out[0], A[0], B[1]);
  and and_16 (Product[0], A[0], B[0]);
endmodule

module ADDER_4_bit (
  input  Cin,
  input  [3:0] A,
  input  [3:0] B,
  output [3:0] S,
  output Cout
);

  wire adder_1bit_1_cout, adder_1bit_2_cout, adder_1bit_3_cout;

  Pull_Resistor pull_resistor_1 (.node(Cin));
  ADDER_1bit adder_1bit_1 (.A(A[0]), .B(B[0]), .Cin(Cin), .S(S[0]), .Cout(adder_1bit_1_cout));
  ADDER_1bit adder_1bit_2 (.A(A[1]), .B(B[1]), .Cin(adder_1bit_1_cout), .S(S[1]), .Cout(adder_1bit_2_cout));
  ADDER_1bit adder_1bit_3 (.A(A[2]), .B(B[2]), .Cin(adder_1bit_2_cout), .S(S[2]), .Cout(adder_1bit_3_cout));
  ADDER_1bit adder_1bit_4 (.A(A[3]), .B(B[3]), .Cin(adder_1bit_3_cout), .S(S[3]), .Cout(Cout));
endmodule

module CMP_8_bit (
  input  [7:0] A,
  input  [7:0] B,
  output GT,
  output EQ,
  output LT
);

  wire and_1_out, and_2_out, cmp_4_bit_1_eq, cmp_4_bit_1_gt, cmp_4_bit_1_lt, cmp_4_bit_2_eq, cmp_4_bit_2_gt,
       cmp_4_bit_2_lt;

  CMP_4_bit cmp_4_bit_1 (.A(A[3:0]), .B(B[3:0]), .GT(cmp_4_bit_1_gt), .EQ(cmp_4_bit_1_eq), .LT(cmp_4_bit_1_lt));
  CMP_4_bit cmp_4_bit_2 (.A(A[7:4]), .B(B[7:4]), .GT(cmp_4_bit_2_gt), .EQ(cmp_4_bit_2_eq), .LT(cmp_4_bit_2_lt));
  and and_1 (and_1_out, cmp_4_bit_1_gt, cmp_4_bit_2_eq);
  and and_2 (and_2_out, cmp_4_bit_1_lt, cmp_4_bit_2_eq);
  or or_1 (GT, and_1_out, cmp_4_bit_2_gt);
  and and_3 (EQ, cmp_4_bit_1_eq, cmp_4_bit_2_eq);
  or or_2 (LT, and_2_out, cmp_4_bit_2_lt);
endmodule

module CMP_4_bit (
  input  [3:0] A,
  input  [3:0] B,
  output GT,
  output EQ,
  output LT
);

  wire and_1_out, and_2_out, cmp_2_bit_1_eq, cmp_2_bit_1_gt, cmp_2_bit_1_lt, cmp_2_bit_2_eq, cmp_2_bit_2_gt,
       cmp_2_bit_2_lt;

  CMP_2_bit cmp_2_bit_1 (.A(A[1:0]), .B(B[1:0]), .GT(cmp_2_bit_1_gt), .EQ(cmp_2_bit_1_eq), .LT(cmp_2_bit_1_lt));
  CMP_2_bit cmp_2_bit_2 (.A(A[3:2]), .B(B[3:2]), .GT(cmp_2_bit_2_gt), .EQ(cmp_2_bit_2_eq), .LT(cmp_2_bit_2_lt));
  and and_1 (and_1_out, cmp_2_bit_1_gt, cmp_2_bit_2_eq);
  and and_2 (and_2_out, cmp_2_bit_1_lt, cmp_2_bit_2_eq);
  or or_1 (GT, and_1_out, cmp_2_bit_2_gt);
  and and_3 (EQ, cmp_2_bit_1_eq, cmp_2_bit_2_eq);
  or or_2 (LT, and_2_out, cmp_2_bit_2_lt);
endmodule

module CMP_2_bit (
  input  [1:0] A,
  input  [1:0] B,
  output GT,
  output EQ,
  output LT
);

  wire and_1_out, and_2_out, cmp_1_bit_1_eq, cmp_1_bit_1_gt, cmp_1_bit_1_lt, cmp_1_bit_2_eq, cmp_1_bit_2_gt,
       cmp_1_bit_2_lt;

  CMP_1_bit cmp_1_bit_1 (.A(A[0]), .B(B[0]), .GT(cmp_1_bit_1_gt), .EQ(cmp_1_bit_1_eq), .LT(cmp_1_bit_1_lt));
  CMP_1_bit cmp_1_bit_2 (.A(A[1]), .B(B[1]), .GT(cmp_1_bit_2_gt), .EQ(cmp_1_bit_2_eq), .LT(cmp_1_bit_2_lt));
  and and_1 (and_1_out, cmp_1_bit_1_gt, cmp_1_bit_2_eq);
  and and_2 (and_2_out, cmp_1_bit_1_lt, cmp_1_bit_2_eq);
  or or_1 (GT, and_1_out, cmp_1_bit_2_gt);
  and and_3 (EQ, cmp_1_bit_1_eq, cmp_1_bit_2_eq);
  or or_2 (LT, and_2_out, cmp_1_bit_2_lt);
endmodule

module CMP_1_bit (
  input  A,
  input  B,
  output GT,
  output EQ,
  output LT
);

  wire not_1_out, not_2_out;

  not not_1 (not_1_out, B);
  not not_2 (not_2_out, A);
  and and_1 (GT, A, not_1_out);
  and and_2 (LT, not_2_out, B);
  nor nor_1 (EQ, GT, LT);
endmodule

module ADDER_1bit (
  input  A,
  input  B,
  input  Cin,
  output S,
  output Cout
);

  wire and_1_out, and_2_out, xor_1_out;

  xor xor_1 (xor_1_out, A, B);
  and and_1 (and_1_out, A, B);
  xor xor_2 (S, xor_1_out, Cin);
  and and_2 (and_2_out, Cin, xor_1_out);
  or or_1 (Cout, and_2_out, and_1_out);
endmodule

module BUS_TERM_DATA (
  input  [15:0] Ain,
  input  [15:0] Zin,
  input  [15:0] Bin,
  input  CLK,
  input  SELECT_1,
  input  SELECT_2,
  input  WE,
  input  OE,
  output [15:0] Aout,
  output [15:0] Zout,
  output [15:0] Bout
);

  wire DECODER_o1, DECODER_o2, DECODER_o3, DECODER_o4;
  wire [15:0] controlled_buffer_1_out, controlled_buffer_4_out, controlled_buffer_7_out,
       controlled_buffer_8_out, controlled_buffer_9_out, TERM_A_q, TERM_B_q;

  DECODER_2x4 DECODER (.A({SELECT_2, SELECT_1}), .O1(DECODER_o1), .O2(DECODER_o2), .O3(DECODER_o3), .O4(DECODER_o4));
  assign controlled_buffer_1_out = DECODER_o2 ? Bin : 16'bz;  // Controlled_Buffer controlled_buffer_1
  assign controlled_buffer_1_out = DECODER_o3 ? Zin : 16'bz;  // Controlled_Buffer controlled_buffer_2
  assign controlled_buffer_1_out = DECODER_o1 ? Ain : 16'bz;  // Controlled_Buffer controlled_buffer_3
  Register #(.width(16)) TERM_A (.D(controlled_buffer_1_out), .en(WE), .clk(CLK), .Q(TERM_A_q));  // open: clr
  Pull_Resistor pull_resistor_1 (.node(controlled_buffer_1_out));
  assign controlled_buffer_4_out = DECODER_o1 ? Bin : 16'bz;  // Controlled_Buffer controlled_buffer_4
  assign controlled_buffer_4_out = DECODER_o3 ? Zin : 16'bz;  // Controlled_Buffer controlled_buffer_5
  assign controlled_buffer_4_out = DECODER_o2 ? Ain : 16'bz;  // Controlled_Buffer controlled_buffer_6
  Pull_Resistor pull_resistor_2 (.node(controlled_buffer_4_out));
  Register #(.width(16)) TERM_B (.D(controlled_buffer_4_out), .en(WE), .clk(CLK), .Q(TERM_B_q));  // open: clr
  assign controlled_buffer_7_out = DECODER_o2 ? TERM_A_q : 16'bz;  // Controlled_Buffer controlled_buffer_7
  assign controlled_buffer_8_out = DECODER_o3 ? TERM_A_q : 16'bz;  // Controlled_Buffer controlled_buffer_8
  assign controlled_buffer_9_out = DECODER_o1 ? TERM_A_q : 16'bz;  // Controlled_Buffer controlled_buffer_9
  assign controlled_buffer_7_out = DECODER_o1 ? TERM_B_q : 16'bz;  // Controlled_Buffer controlled_buffer_10
  assign controlled_buffer_8_out = DECODER_o4 ? TERM_B_q : 16'bz;  // Controlled_Buffer controlled_buffer_11
  assign controlled_buffer_9_out = DECODER_o2 ? TERM_B_q : 16'bz;  // Controlled_Buffer controlled_buffer_12
  assign Aout = OE ? controlled_buffer_9_out : 16'bz;  // Controlled_Buffer controlled_buffer_13
  assign Zout = OE ? controlled_buffer_8_out : 16'bz;  // Controlled_Buffer controlled_buffer_14
  assign Bout = OE ? controlled_buffer_7_out : 16'bz;  // Controlled_Buffer controlled_buffer_15

  // Notes on the sheet:
  //   SWAP MEM: TERM_A outputs to Bout; TERM_B to Aout
  //   SWAP REG: TERM_A takes input from Bin, and TERM_B takes input from Ain
  //   SWAP REG: TERM_A outputs to Aout, TERM_B outputs to Bout
  //   BLOCK STORE: TERM_B takes input from Bin, outputs to Zout
  //   MOVE MEM: TERM_A takes input from Zin, outputs to Aout
  //   MOVE MEM: TERM_B takes input from Zin, outputs to Bout
  //   SWAP MEM: TERM_A takes input from Ain; TERM_B from Bin
  //   BS=00
  //   BS=01
  //   BS=10 Take middle as input: A takes Zin.
  //   BS=10 Output to middle: A outputs Zout
  //   BS=11 Take middle as input: B takes Zin.
  //   BS=11 Output to middle: B outputs Zout.
  //   BS=00 Take normal input, A takes Ain; B takes Bin.
  //   BS=00 Normal Output; A outputs Aout; B outputs Bout
  //   BS=01 Take inverted inputs; A takes Bin; B takes Ain
  //   BS=01 Inverted Outputs: A outputs Bout; B outputs Aout
endmodule

module REG_SWAP_EXPLAIN (
  input  [4:0] AddrB,
  input  [4:0] AddrA,
  input  OE_SWAP_REG,
  input  WE_SWAP_REG,
  output out_5,
  output out_6,
  output out_7,
  output out_8,
  output out_9,
  output out_10,
  output out_11,
  output out_12,
  output out_13,
  output out_14,
  output out_15,
  output out_16,
  output out_17,
  output out_18,
  output out_19,
  output out_20
);

  wire decoder_2x4_1_o1, decoder_2x4_1_o2, decoder_2x4_1_o3, decoder_2x4_1_o4, decoder_2x4_2_o1,
       decoder_2x4_2_o2, decoder_2x4_2_o3, decoder_2x4_2_o4;

  DECODER_2x4 decoder_2x4_1 (
    .A(AddrB[1:0]), .O1(decoder_2x4_1_o1), .O2(decoder_2x4_1_o2), .O3(decoder_2x4_1_o3), .O4(decoder_2x4_1_o4));
  DECODER_2x4 decoder_2x4_2 (
    .A(AddrA[1:0]), .O1(decoder_2x4_2_o1), .O2(decoder_2x4_2_o2), .O3(decoder_2x4_2_o3), .O4(decoder_2x4_2_o4));
  assign out_5 = OE_SWAP_REG ? decoder_2x4_1_o4 : 1'bz;  // Controlled_Buffer controlled_buffer_1
  assign out_6 = WE_SWAP_REG ? decoder_2x4_1_o4 : 1'bz;  // Controlled_Buffer controlled_buffer_2
  assign out_7 = OE_SWAP_REG ? decoder_2x4_1_o3 : 1'bz;  // Controlled_Buffer controlled_buffer_3
  assign out_8 = WE_SWAP_REG ? decoder_2x4_1_o3 : 1'bz;  // Controlled_Buffer controlled_buffer_4
  assign out_9 = OE_SWAP_REG ? decoder_2x4_1_o2 : 1'bz;  // Controlled_Buffer controlled_buffer_5
  assign out_10 = WE_SWAP_REG ? decoder_2x4_1_o2 : 1'bz;  // Controlled_Buffer controlled_buffer_6
  assign out_11 = OE_SWAP_REG ? decoder_2x4_1_o1 : 1'bz;  // Controlled_Buffer controlled_buffer_7
  assign out_12 = WE_SWAP_REG ? decoder_2x4_1_o1 : 1'bz;  // Controlled_Buffer controlled_buffer_8
  assign out_13 = OE_SWAP_REG ? decoder_2x4_2_o4 : 1'bz;  // Controlled_Buffer controlled_buffer_9
  assign out_14 = WE_SWAP_REG ? decoder_2x4_2_o4 : 1'bz;  // Controlled_Buffer controlled_buffer_10
  assign out_15 = OE_SWAP_REG ? decoder_2x4_2_o3 : 1'bz;  // Controlled_Buffer controlled_buffer_11
  assign out_16 = WE_SWAP_REG ? decoder_2x4_2_o3 : 1'bz;  // Controlled_Buffer controlled_buffer_12
  assign out_17 = OE_SWAP_REG ? decoder_2x4_2_o2 : 1'bz;  // Controlled_Buffer controlled_buffer_13
  assign out_18 = WE_SWAP_REG ? decoder_2x4_2_o2 : 1'bz;  // Controlled_Buffer controlled_buffer_14
  assign out_19 = OE_SWAP_REG ? decoder_2x4_2_o1 : 1'bz;  // Controlled_Buffer controlled_buffer_15
  assign out_20 = WE_SWAP_REG ? decoder_2x4_2_o1 : 1'bz;  // Controlled_Buffer controlled_buffer_16
  Pull_Resistor pull_resistor_1 (.node(out_5));
  Pull_Resistor pull_resistor_2 (.node(out_6));
  Pull_Resistor pull_resistor_3 (.node(out_7));
  Pull_Resistor pull_resistor_4 (.node(out_8));
  Pull_Resistor pull_resistor_5 (.node(out_9));
  Pull_Resistor pull_resistor_6 (.node(out_10));
  Pull_Resistor pull_resistor_7 (.node(out_13));
  Pull_Resistor pull_resistor_8 (.node(out_14));
  Pull_Resistor pull_resistor_9 (.node(out_15));
  Pull_Resistor pull_resistor_10 (.node(out_16));
  Pull_Resistor pull_resistor_11 (.node(out_17));
  Pull_Resistor pull_resistor_12 (.node(out_18));
  Pull_Resistor pull_resistor_13 (.node(out_11));
  Pull_Resistor pull_resistor_14 (.node(out_12));
  Pull_Resistor pull_resistor_15 (.node(out_19));
  Pull_Resistor pull_resistor_16 (.node(out_20));
endmodule
